# Fritzing sketch gardenpi_schematics (saved by Fritzing 0.9.6b)
breadboards: 1

parts:
  Stepdown_Voltage1 = Polulu Stepdown Voltage [part_number=D24V25F3,D24V25F5]
  LED1 = LED - 5mm [color="Blue (430nm)" current=0.030 package="5 mm [THT]"]
  U1 = 2-Channel 5v Relay Shield [package=relay-2ch5v10a]
  MCU1 = Raspberry Pi Zero
  J1 = Camdenboss CTB0158-2 [part_number=CTB0158-2 package=THT]
  LED2 = LED - 5mm [color="Blue (430nm)" current=0.030 package="5 mm [THT]"]
  J3 = Camdenboss CTB0158-2 [part_number=CTB0158-2 package=THT]
  J4 = Camdenboss CTB0158-2 [part_number=CTB0158-2 package=THT]
  ZS-042_RTC1 = ZS-042 RTC Module
  BULB1 = LEDs [package=led10mm]
  BULB2 = LEDs [package=led10mm]
  R2 = Resistor [tolerance=±5% power=0.25 resistance=1.2k package=THT]
  J5 = Piezo Speaker
  S1 = Round Pushbutton
  R3 = Resistor [tolerance=±5% resistance=10k package="2512 [SMD]"]
  R4 = Resistor [tolerance=±5% resistance=1.2k package="2010 [SMD]"]
  S2 = Round Pushbutton  # not connected

nets:
  N1: Stepdown_Voltage1.VIn, J1.pin1, J3.pin2, J4.pin2
  GND: Stepdown_Voltage1.GND, U1.GND, MCU1.pin_6, MCU1.pin_9, MCU1.pin_14, MCU1.pin_34, J1.pin2, J3.pin1, J4.pin1, ZS-042_RTC1.GND, R2.Pin_0, J5.pin2, S1.leg1
  N2: Stepdown_Voltage1.VOut, U1.VCC, MCU1.pin_4, R3.Pin_0
  N3: LED1.anode, R4.Pin_1
  N4: U1.IN1, MCU1.pin_12
  N5: U1.IN2, MCU1.pin_16
  N6: U1.K1-In, BULB2.C
  N7: U1.K1-On, J4.terminal_2
  N8: U1.K2-In, BULB1.C
  N9: U1.K2-On, J3.terminal_2
  N10: MCU1.pin_1, MCU1.pin_17, ZS-042_RTC1.VCC
  N11: MCU1.pin_3, ZS-042_RTC1.SDA
  N12: MCU1.pin_5, ZS-042_RTC1.SCL
  N13: MCU1.pin_8, LED2.cathode
  N14: MCU1.pin_10, S1.leg0, R3.Pin_1
  N15: MCU1.pin_40, J5.pin1
  N16: LED2.anode, R2.Pin_1
  N17: J3.terminal_1, BULB1.A
  N18: J4.terminal_1, BULB2.A

notes:
  DC Input: 12V
  Door switch SW1
  Main Channel REL1
  Second Channel REL2
  Door switch LED indicator
  Pi Reset Indicator
  RST/HLT Button
  Connected to Run port on Pi

custom parts:
  Polulu Stepdown Voltage: Polulu Stepdown Voltage 3V3 or 5V, 2.5A
  2-Channel 5v Relay Shield: 2 Channel 5v Relay Shield w. 2x SPD-06VDC-SD-C
